# Fritzing sketch WhatsApp_Surveillance_Camera (saved by Fritzing 0.9.3b)
breadboards: 1

parts:
  Raspberry_Pi1 = Raspberry Pi B+
  CAMERA1 = TTL Serial JPEG Camera  # not connected
  Part1 = Arduino Nano (Rev3.0)
  J3 = Infrared Proximity Sensor
  R1 = Photocell (LDR) [package=THT]
  LED1 = smd LED [color="Red (633nm)" package="0805 [SMD]"]
  LED2 = smd LED [color="Red (633nm)" package="0805 [SMD]"]
  R2 = Resistor [tolerance=±5% resistance=220 package="2010 [SMD]"]
  R3 = Resistor [tolerance=±5% resistance=220 package="2010 [SMD]"]
  R4 = Resistor [tolerance=±5% resistance=220 package="2010 [SMD]"]
  R5 = Resistor [tolerance=±5% resistance=220 package="2010 [SMD]"]
  R6 = Resistor [tolerance=±5% resistance=220 package="2010 [SMD]"]

nets:
  N1: Raspberry_Pi1.GPIO22, LED1.anode, R2.Pin_1, R3.Pin_0
  N2: Raspberry_Pi1.GPIO23, LED2.anode, R4.Pin_1, R5.Pin_0
  GND: Raspberry_Pi1.GND, Part1.GND, J3.GND, LED1.cathode, LED2.cathode, R2.Pin_0, R4.Pin_0, R6.Pin_0
  5V: Raspberry_Pi1.5V, Part1.VIN
  N3: Part1.D3, R3.Pin_1
  N4: Part1.D4, R5.Pin_1
  5V_2: Part1.5V, J3.Vcc, R1.pin_1
  N5: Part1.A1, R1.pin_0, R6.Pin_1
  N6: Part1.A0, J3.Vout

custom parts:
  TTL Serial JPEG Camera: TTL Serial JPEG Camera with NTSC Out
